// Logisim project Processor.circ as structural Verilog: 6 circuits, main circuit main
// REGISTERS
module Register_File (
  input  dstM,
  input  [1:0] rA,
  input  [7:0] valM,
  input  [1:0] rB,
  output [7:0] eax,
  output [7:0] valA,
  output [7:0] ebx,
  output Zero,
  output [7:0] ecx,
  output [7:0] edx,
  output Negative,
  output [7:0] valB
);

  wire clock_1_out, demultiplexer_1_out0, demultiplexer_1_out1, demultiplexer_1_out2, demultiplexer_1_out3,
       or_1_out;

  Demultiplexer #(.select(2), .enable("false")) demultiplexer_1 (
    .out0(demultiplexer_1_out0), .out1(demultiplexer_1_out1), .out2(demultiplexer_1_out2),
    .out3(demultiplexer_1_out3), .in(dstM), .sel(rA));
  Clock clock_1 (.out(clock_1_out));
  Register register_1 (.D(valM), .en(demultiplexer_1_out0), .Q(eax), .clk(clock_1_out));  // open: clr
  Register register_2 (.D(valM), .en(demultiplexer_1_out1), .Q(ebx), .clk(clock_1_out));  // open: clr
  Register register_3 (.D(valM), .en(demultiplexer_1_out2), .Q(ecx), .clk(clock_1_out));  // open: clr
  Register register_4 (.D(valM), .en(demultiplexer_1_out3), .Q(edx), .clk(clock_1_out));  // open: clr
  Multiplexer #(.select(2), .width(8), .enable("false")) multiplexer_1 (
    .in0(eax), .in1(ebx), .in2(ecx), .in3(edx), .out({Negative, valA[6:0]}), .sel(rA));
  Multiplexer #(.select(2), .width(8), .enable("false")) multiplexer_2 (
    .in0(eax), .in1(ebx), .in2(ecx), .in3(edx), .out(valB), .sel(rB));
  or or_1 (or_1_out, valA[0], valA[1], valA[2], valA[3], valA[4], valA[5], valA[6], Negative);
  not not_1 (Zero, or_1_out);

  assign valA[7] = Negative;

  // Notes on the sheet:
  //   drs
endmodule

module main (
  output [7:0] address,
  output [7:0] valM,
  output [1:0] addrsel,
  output [7:0] valE,
  output [1:0] icode,
  output [7:0] valA,
  output [7:0] valB,
  output [7:0] eax,
  output [7:0] ebx,
  output [7:0] valC,
  output [7:0] ecx,
  output [7:0] edx,
  output [7:0] valM_2,
  output pcsel,
  output pcload,
  output [1:0] ifun
);

  wire and_1_out, button_1_out, clock_1_out, comparator_1_eq, decoder_1_dstm, decoder_1_irmovl,
       decoder_1_readwrite, decoder_1_rmmovl, register_file_1_negative, register_file_1_zero, t_ff_1_q;
  wire [1:0] decoder_1_ra, decoder_1_rb, decoder_1_regsel;
  wire [7:0] multiplexer_1_out, multiplexer_3_out, pc_adder_1_pc_out, register_1_q, register_2_q,
       register_3_q;

  Multiplexer #(.width(8)) multiplexer_1 (
    .in0(address), .in1(8'ha8), .out(multiplexer_1_out), .sel(comparator_1_eq));  // open: en
  Button button_1 (.out(button_1_out));
  Comparator comparator_1 (.a(register_2_q), .b(8'h70), .eq(comparator_1_eq));  // open: gt, lt
  RAM #(.bus("separate")) ram_1 (
    .addr(multiplexer_1_out), .din(valA), .data(valC), .str(decoder_1_readwrite), .clk(and_1_out));  // open: sel, ld, clr
  T_Flip_Flop t_ff_1 (
    .clk(clock_1_out), .T(button_1_out), .Q(t_ff_1_q), .reset(comparator_1_eq), .en(clock_1_out));  // open: Qn, preset
  Clock clock_1 (.out(clock_1_out));
  Multiplexer #(.select(2), .width(8), .enable("false")) multiplexer_2 (
    .in0(register_3_q), .in1(register_1_q), .in2(valB), .in3(valA), .out(address), .sel(addrsel));
  Register register_1 (.D(valC), .en(decoder_1_rmmovl), .Q(register_1_q), .clk(and_1_out));  // open: clr
  Register register_2 (.D(valC), .en(decoder_1_irmovl), .Q(register_2_q), .clk(and_1_out));  // open: clr
  and and_1 (and_1_out, t_ff_1_q, clock_1_out);
  Decoder decoder_1 (
    .addrsel(addrsel), .irvalue(register_2_q), .irmovl(decoder_1_irmovl), .rmmovl(decoder_1_rmmovl),
    .dstM(decoder_1_dstm), .rA(decoder_1_ra), .rB(decoder_1_rb), .icode(icode), .regsel(decoder_1_regsel),
    .ifun(ifun), .readwrite(decoder_1_readwrite), .pcsel(pcsel), .zero(register_file_1_zero),
    .negative(register_file_1_negative), .pcload(pcload));
  Multiplexer #(.width(8), .enable("false")) multiplexer_3 (
    .in0(register_1_q), .in1(pc_adder_1_pc_out), .out(multiplexer_3_out), .sel(pcsel));
  PC_Adder pc_adder_1 (.PC_in(register_3_q), .PC_out(pc_adder_1_pc_out));
  Register register_3 (.D(multiplexer_3_out), .en(pcload), .Q(register_3_q), .clk(and_1_out));  // open: clr
  ALU alu_1 (.valA(valA), .valB(valB), .val_E(valE), .ifun(icode));
  Register_File register_file_1 (
    .valA(valA), .valB(valB), .rA(decoder_1_ra), .rB(decoder_1_rb), .valM(valM), .dstM(decoder_1_dstm),
    .eax(eax), .ebx(ebx), .ecx(ecx), .edx(edx), .Zero(register_file_1_zero),
    .Negative(register_file_1_negative));
  Multiplexer #(.select(2), .width(8), .enable("false")) multiplexer_4 (
    .in0(register_1_q), .in1(valB), .in2(valC), .in3(valE), .out(valM), .sel(decoder_1_regsel));

  assign valM_2 = valM;
endmodule

// PC
module PC_Adder (
  input  [7:0] PC_in,
  output [7:0] PC_out
);

  Adder adder_1 (.a(PC_in), .b(8'h1), .out(PC_out), .cin(1'b0));  // open: cout
endmodule

// DECODE
module Decoder (
  input  [7:0] irvalue,
  input  zero,
  input  negative,
  output [1:0] ifun,
  output [1:0] rB,
  output [1:0] rA,
  output [1:0] icode,
  output irmovl,
  output rmmovl,
  output pcsel,
  output readwrite,
  output pcload,
  output [1:0] regsel,
  output dstM,
  output [1:0] addrsel
);

  wire and_1_out, and_2_out, and_3_out, and_4_out, and_5_out, clock_1_out, multiplexer_3_out,
       multiplexer_7_out, not_1_out, not_2_out, not_3_out, not_4_out, or_1_out;
  wire [1:0] multiplexer_1_out, multiplexer_11_out;

  not not_1 (not_1_out, zero);
  not not_2 (not_2_out, negative);
  and and_1 (and_1_out, not_1_out, not_2_out);
  Multiplexer #(.select(4), .width(2), .enable("false")) multiplexer_1 (
    .in0(2'b11), .in1(2'b11), .in2(2'b11), .in3(2'b11), .in4(2'b10), .in5(2'b00), .in6(2'b01), .in7(2'b00),
    .in8(2'b00), .in9(2'b00), .in10(2'b00), .in11(2'b00), .in12(2'b10), .in13(2'b00), .in14(2'b00),
    .in15(2'b00), .out(multiplexer_1_out), .sel(irvalue[7:4]));
  Multiplexer #(.select(2), .enable("false")) multiplexer_2 (
    .in0(1'b1), .in1(1'b0), .in2(1'b0), .in3(1'b0), .out(irmovl), .sel(ifun));
  not not_3 (not_3_out, irvalue[6]);
  Multiplexer #(.select(2), .enable("false")) multiplexer_3 (
    .in0(zero), .in1(not_1_out), .in2(and_1_out), .in3(negative), .out(multiplexer_3_out), .sel(irvalue[5:4]));
  and and_2 (and_2_out, not_3_out, irvalue[7], multiplexer_3_out);
  and and_3 (and_3_out, irvalue[4], irvalue[5], irvalue[6], irvalue[7]);
  Multiplexer #(.select(2), .width(2), .enable("false")) multiplexer_4 (
    .in0(2'b00), .in1(2'b00), .in2(multiplexer_1_out), .in3(2'b00), .out(regsel), .sel(ifun));
  or or_1 (or_1_out, and_2_out, and_3_out);
  Multiplexer #(.select(2), .enable("false")) multiplexer_5 (
    .in0(1'b1), .in1(irvalue[7]), .in2(or_1_out), .in3(1'b0), .out(pcload), .sel(ifun));
  Multiplexer #(.select(2), .enable("false")) multiplexer_6 (
    .in0(1'b0), .in1(irvalue[7]), .in2(1'b0), .in3(1'b0), .out(rmmovl), .sel(ifun));
  Multiplexer #(.select(4), .enable("false")) multiplexer_7 (
    .in0(1'b1), .in1(1'b1), .in2(1'b1), .in3(1'b1), .in4(1'b1), .in5(1'b0), .in6(1'b1), .in7(1'b0),
    .in8(1'b0), .in9(1'b0), .in10(1'b0), .in11(1'b0), .in12(1'b1), .in13(1'b0), .in14(1'b1), .in15(1'b0),
    .out(multiplexer_7_out), .sel(irvalue[7:4]));
  Counter #(.width(2), .max('h3)) counter_1 (
    .Q(ifun), .clk(clock_1_out), .clr(and_4_out));  // open: load, D, count, carry
  and and_4 (and_4_out, ifun[1], ifun[0]);
  Clock clock_1 (.out(clock_1_out));
  not not_4 (not_4_out, irvalue[5]);
  Multiplexer #(.select(2), .enable("false")) multiplexer_8 (
    .in0(1'b0), .in1(1'b0), .in2(multiplexer_7_out), .in3(1'b0), .out(dstM), .sel(ifun));
  Multiplexer #(.select(2), .enable("false")) multiplexer_9 (
    .in0(1'b1), .in1(1'b1), .in2(1'b0), .in3(1'b0), .out(pcsel), .sel(ifun));
  and and_5 (and_5_out, irvalue[4], not_4_out, irvalue[6]);
  Multiplexer #(.select(2), .enable("false")) multiplexer_10 (
    .in0(1'b0), .in1(1'b0), .in2(and_5_out), .in3(1'b0), .out(readwrite), .sel(ifun));
  Multiplexer #(.select(4), .width(2), .enable("false")) multiplexer_11 (
    .in0(2'b00), .in1(2'b00), .in2(2'b00), .in3(2'b00), .in4(2'b10), .in5(2'b10), .in6(2'b00), .in7(2'b00),
    .in8(2'b00), .in9(2'b00), .in10(2'b00), .in11(2'b00), .in12(2'b00), .in13(2'b01), .in14(2'b01),
    .in15(2'b00), .out(multiplexer_11_out), .sel(irvalue[7:4]));
  Multiplexer #(.select(2), .width(2), .enable("false")) multiplexer_12 (
    .in0(2'b00), .in1(2'b00), .in2(multiplexer_11_out), .in3(2'b00), .out(addrsel), .sel(ifun));

  assign icode = irvalue[5:4];
  assign rA = irvalue[3:2];
  assign rB = irvalue[1:0];

  // Notes on the sheet:
  //   op1op2
  //   op2
endmodule

module ALU (
  input  [1:0] ifun,
  input  [7:0] valA,
  input  [7:0] valB,
  output [7:0] val_E
);

  wire alu_add_1_carry_out, alu_add_2_carry_out, alu_add_3_carry_out, alu_add_4_carry_out,
       alu_add_5_carry_out, alu_add_6_carry_out, alu_add_7_carry_out;

  ALU_ADD alu_add_1 (
    .bit_A(valA[0]), .bit_B(valB[0]), .Carry_In(ifun[1]), .Carry_Out(alu_add_1_carry_out), .bit_E(val_E[0]));
  ALU_ADD alu_add_2 (
    .bit_A(valA[1]), .bit_B(valB[1]), .Carry_In(alu_add_1_carry_out), .Carry_Out(alu_add_2_carry_out),
    .bit_E(val_E[1]));
  ALU_ADD alu_add_3 (
    .bit_A(valA[2]), .bit_B(valB[2]), .Carry_In(alu_add_2_carry_out), .Carry_Out(alu_add_3_carry_out),
    .bit_E(val_E[2]));
  ALU_ADD alu_add_4 (
    .bit_A(valA[3]), .bit_B(valB[3]), .Carry_In(alu_add_3_carry_out), .Carry_Out(alu_add_4_carry_out),
    .bit_E(val_E[3]));
  ALU_ADD alu_add_5 (
    .bit_A(valA[4]), .bit_B(valB[4]), .Carry_In(alu_add_4_carry_out), .Carry_Out(alu_add_5_carry_out),
    .bit_E(val_E[4]));
  ALU_ADD alu_add_6 (
    .bit_A(valA[5]), .bit_B(valB[5]), .Carry_In(alu_add_5_carry_out), .Carry_Out(alu_add_6_carry_out),
    .bit_E(val_E[5]));
  ALU_ADD alu_add_7 (
    .bit_A(valA[6]), .bit_B(valB[6]), .Carry_In(alu_add_6_carry_out), .Carry_Out(alu_add_7_carry_out),
    .bit_E(val_E[6]));
  ALU_ADD alu_add_8 (
    .bit_A(valA[7]), .bit_B(valB[7]), .Carry_In(alu_add_7_carry_out), .bit_E(val_E[7]));  // open: Carry_Out
endmodule

// ADD
module ALU_ADD (
  input  Carry_In,
  input  bit_A,
  input  bit_B,
  output bit_E,
  output Carry_Out
);

  wire and_1_out, and_2_out, xor_1_out;

  and and_1 (and_1_out, bit_A, bit_B);
  xor xor_1 (xor_1_out, bit_A, bit_B);
  or or_1 (Carry_Out, and_1_out, and_2_out);
  and and_2 (and_2_out, Carry_In, xor_1_out);
  xor xor_2 (bit_E, Carry_In, xor_1_out);
endmodule
