// Logisim project Part 1.circ as structural Verilog: 1 circuit, main circuit main
module main (
  input  a,
  input  b,
  input  c,
  output F,
  output G
);

  wire and_1_out, and_2_out, and_3_out, and_4_out, and_5_out, and_6_out, and_7_out, and_8_out, and_9_out,
       not_1_out, not_2_out, not_3_out, or_1_out, or_2_out, or_3_out, or_4_out;

  and and_1 (and_1_out, a, b);
  not not_1 (not_1_out, a);
  not not_2 (not_2_out, b);
  not not_3 (not_3_out, b);
  and and_2 (and_2_out, and_1_out, c);
  and and_3 (and_3_out, a, b);
  and and_4 (and_4_out, not_1_out, not_2_out);
  and and_5 (and_5_out, a, not_3_out);
  or or_1 (or_1_out, and_2_out, and_3_out);
  and and_6 (and_6_out, and_4_out, c);
  and and_7 (and_7_out, and_5_out, c);
  and and_8 (and_8_out, a, b);
  or or_2 (or_2_out, or_1_out, a);
  or or_3 (or_3_out, b, c);
  or or_4 (or_4_out, and_6_out, and_7_out);
  and and_9 (and_9_out, and_8_out, c);
  or or_5 (F, or_2_out, or_3_out);
  or or_6 (G, or_4_out, and_9_out);
endmodule
