// Logisim project Part 2.circ as structural Verilog: 1 circuit, main circuit main
module main (
  input  I0,
  input  A,
  input  I1,
  input  B,
  input  C,
  input  I2,
  input  D,
  input  I3,
  input  E,
  input  I4,
  input  F,
  input  G,
  input  I5,
  input  I6,
  input  DP,
  input  I7,
  input  o1,
  input  d0,
  input  d1,
  input  d2,
  input  o2,
  input  o3,
  input  o4,
  input  o5,
  input  o6,
  input  o7,
  input  o8,
  input  DP_2,
  input  I0_2,
  input  CAR_1__MOTOR_CAR,
  input  I1_2,
  input  I2_2,
  input  I3_2,
  input  I4_2,
  input  I5_2,
  input  I6_2,
  input  DP_3,
  output d0_2,
  output d1_2,
  output d2_2,
  output o1_2,
  output o2_2,
  output o3_2,
  output o4_2,
  output o5_2,
  output o6_2,
  output o7_2,
  output o8_2
);

  wire and_9_out, and_10_out, and_11_out, and_12_out, and_13_out, and_14_out, and_15_out, and_16_out,
       not_1_out, not_2_out, not_3_out, not_4_out, not_5_out, not_6_out, or_4_out, or_5_out, or_6_out,
       or_7_out, or_8_out, or_9_out, or_10_out, or_11_out, or_12_out, or_13_out, or_14_out, or_15_out,
       or_16_out, or_17_out, or_18_out, or_19_out, or_20_out, or_21_out, or_22_out;

  not not_1 (not_1_out, d0);
  not not_2 (not_2_out, d1);
  or or_1 (d0_2, I4, I5, I6, I7);
  or or_2 (d1_2, I2, I3, I7, I6);
  or or_3 (d2_2, I1, I3, I5, I7);
  not not_3 (not_3_out, d2);
  and and_1 (o1_2, not_1_out, not_2_out, not_3_out);
  and and_2 (o2_2, not_1_out, not_2_out, d2);
  and and_3 (o3_2, d1, not_1_out, not_3_out);
  and and_4 (o4_2, not_1_out, d1, d2);
  and and_5 (o5_2, d0, not_2_out, not_3_out);
  and and_6 (o6_2, d0, not_2_out, d2);
  and and_7 (o7_2, d0, d1, not_3_out);
  and and_8 (o8_2, d0, d1, d2);
  _7_Segment_Display u_7_segment_display_1 (.g(G), .f(F), .a(A), .b(B), .e(E), .d(D), .c(C), .dp(DP));
  or or_4 (or_4_out, o7, o3, o4, o6, o8, o1);
  or or_5 (or_5_out, o4, o5, o2, o3, o8, o1);
  or or_6 (or_6_out, o2, o5, o6, o4, o7, o1, o8);
  or or_7 (or_7_out, o3, o4, o7, o6, o1);
  or or_8 (or_8_out, o7, o3, o1);
  or or_9 (or_9_out, o5, o6, o7, o1);
  or or_10 (or_10_out, o5, o3, o4, o6, o7);
  buf or_11 (or_11_out, DP_2);  // OR_Gate
  or or_12 (or_12_out, I3_2, I4_2, I5_2, I6_2);
  or or_13 (or_13_out, I1_2, I2_2, I6_2, I5_2);
  or or_14 (or_14_out, CAR_1__MOTOR_CAR, I2_2, I4_2, I6_2);
  not not_4 (not_4_out, or_12_out);
  not not_5 (not_5_out, or_13_out);
  not not_6 (not_6_out, or_14_out);
  _7_Segment_Display u_7_segment_display_2 (
    .g(or_10_out), .f(or_9_out), .a(or_4_out), .b(or_5_out), .e(or_8_out), .d(or_7_out), .c(or_6_out),
    .dp(or_11_out));
  and and_9 (and_9_out, not_4_out, not_5_out, not_6_out);
  and and_10 (and_10_out, not_4_out, not_5_out, or_14_out);
  and and_11 (and_11_out, or_13_out, not_4_out, not_6_out);
  and and_12 (and_12_out, not_4_out, or_13_out, or_14_out);
  and and_13 (and_13_out, or_12_out, not_5_out, not_6_out);
  and and_14 (and_14_out, or_12_out, not_5_out, or_14_out);
  and and_15 (and_15_out, or_12_out, or_13_out, not_6_out);
  and and_16 (and_16_out, or_12_out, or_13_out, or_14_out);
  or or_15 (or_15_out, and_15_out, and_11_out, and_12_out, and_14_out, and_16_out, and_9_out);
  or or_16 (or_16_out, and_12_out, and_13_out, and_10_out, and_11_out, and_16_out, and_9_out);
  or or_17 (or_17_out, and_10_out, and_13_out, and_14_out, and_12_out, and_15_out, and_9_out, and_16_out);
  or or_18 (or_18_out, and_11_out, and_12_out, and_15_out, and_14_out, and_9_out);
  or or_19 (or_19_out, and_15_out, and_11_out, and_9_out);
  or or_20 (or_20_out, and_13_out, and_14_out, and_15_out, and_9_out);
  or or_21 (or_21_out, and_13_out, and_11_out, and_12_out, and_14_out, and_15_out);
  buf or_22 (or_22_out, DP_3);  // OR_Gate
  _7_Segment_Display u_7_segment_display_3 (
    .g(or_21_out), .f(or_20_out), .a(or_15_out), .b(or_16_out), .e(or_19_out), .d(or_18_out), .c(or_17_out),
    .dp(or_22_out));

  // Notes on the sheet:
  //   ENCODER
  //   DECODER
  //   7 SEGMENT DISPLAY SET UP
  //   CAR 2
  //   CAR 3
  //   CAR 4
  //   CAR 5
  //   CAR 6
  //   CAR 7
  //   I7
  //   HOW TO CONNECT DECODER TO THE DISPLAY
  //   A
  //   B
  //   C
  //   D
  //   E
  //   F
  //   G
  //   DP
  //   COMPLETE CIRCUIT WITH DISPLAY- ENCODER - DECODER
  //   A
  //   B
  //   C
  //   D
  //   E
  //   F
  //   G
  //   DP
endmodule
