// Logisim project Problem 3.circ as structural Verilog: 2 circuits, main circuit main
module main (
  input  I_O,
  input  A0,
  input  A1,
  input  A2,
  input  A3,
  output out_6,
  output A_C,
  output D0,
  output D1,
  output D2,
  output D3,
  output ENGINE,
  output WIPPERS
);

  wire _0_out, _1_out, _2_out, _3_out, _4_out, _5_out, _6_out, clock_1_out, clock_2_out, clock_3_out,
       clock_4_out, clock_5_out, clock_6_out, clock_7_out, clock_8_out, nand_1_out, nand_2_out, nand_4_out,
       nand_5_out, nand_6_out, nand_7_out, nand_8_out, nand_9_out, nand_10_out, nand_11_out, nand_12_out,
       nand_13_out, nand_14_out, nand_15_out, nand_16_out, nand_17_out, nand_18_out, nand_20_out,
       nand_22_out, nand_24_out, nand_26_out, nand_28_out, nand_30_out, nand_32_out, not_1_out, not_2_out,
       not_3_out, not_4_out;

  nand nand_1 (nand_1_out, nand_4_out, clock_1_out);
  Clock clock_1 (.out(clock_1_out));
  nand nand_2 (nand_2_out, clock_1_out, out_6);
  nand nand_3 (out_6, nand_1_out, nand_4_out);
  nand nand_4 (nand_4_out, out_6, nand_2_out);
  not not_1 (not_1_out, A0);
  not not_2 (not_2_out, A3);
  not not_3 (not_3_out, A1);
  not not_4 (not_4_out, A2);
  and _0 (_0_out, not_1_out, not_3_out, not_4_out, not_2_out, I_O);
  and _1 (_1_out, A0, not_3_out, not_4_out, not_2_out, I_O);
  and _2 (_2_out, not_1_out, A1, not_4_out, not_2_out, I_O);
  and _3 (_3_out, A0, A1, not_4_out, not_2_out, I_O);
  and _4 (_4_out, not_1_out, not_3_out, A2, not_2_out, I_O);
  and _5 (_5_out, A0, not_3_out, A2, not_2_out, I_O);
  and _6 (_6_out, not_1_out, A1, A2, not_2_out, I_O);
  Clock clock_2 (.out(clock_2_out));
  Clock clock_3 (.out(clock_3_out));
  nand nand_5 (nand_5_out, nand_20_out, _0_out, clock_2_out);
  nand nand_6 (nand_6_out, clock_2_out, A3, A_C);
  nand nand_7 (nand_7_out, nand_22_out, _1_out, clock_3_out);
  nand nand_8 (nand_8_out, clock_3_out, A3, D0);
  nand nand_9 (nand_9_out, nand_24_out, _2_out, clock_4_out);
  Clock clock_4 (.out(clock_4_out));
  nand nand_10 (nand_10_out, clock_4_out, A3, D1);
  nand nand_11 (nand_11_out, nand_26_out, _3_out, clock_5_out);
  Clock clock_5 (.out(clock_5_out));
  nand nand_12 (nand_12_out, clock_5_out, A3, D2);
  nand nand_13 (nand_13_out, nand_28_out, _4_out, clock_6_out);
  Clock clock_6 (.out(clock_6_out));
  nand nand_14 (nand_14_out, clock_6_out, A3, D3);
  nand nand_15 (nand_15_out, nand_30_out, _5_out, clock_7_out);
  Clock clock_7 (.out(clock_7_out));
  nand nand_16 (nand_16_out, clock_7_out, A3, ENGINE);
  nand nand_17 (nand_17_out, nand_32_out, _6_out, clock_8_out);
  Clock clock_8 (.out(clock_8_out));
  nand nand_18 (nand_18_out, clock_8_out, A3, WIPPERS);
  nand nand_19 (A_C, nand_5_out, nand_20_out);
  nand nand_20 (nand_20_out, A_C, nand_6_out);
  nand nand_21 (D0, nand_7_out, nand_22_out);
  nand nand_22 (nand_22_out, D0, nand_8_out);
  nand nand_23 (D1, nand_9_out, nand_24_out);
  nand nand_24 (nand_24_out, D1, nand_10_out);
  nand nand_25 (D2, nand_11_out, nand_26_out);
  nand nand_26 (nand_26_out, D2, nand_12_out);
  nand nand_27 (D3, nand_13_out, nand_28_out);
  nand nand_28 (nand_28_out, D3, nand_14_out);
  nand nand_29 (ENGINE, nand_15_out, nand_30_out);
  nand nand_30 (nand_30_out, ENGINE, nand_16_out);
  nand nand_31 (WIPPERS, nand_17_out, nand_32_out);
  nand nand_32 (nand_32_out, WIPPERS, nand_18_out);

  // Notes on the sheet:
  //   AFTER RESET
  //   REWIRE THIS WIRE INPUT INTO NAND
  //   >>>>>>>>>>>>>>>>>>>>>>>>>>>>>>>>>>>>
  //   A3 - RESET BUTTON
  //   EXAMPLE FOR LARGER PICTURE
  //   WORKING EXAMPLE
endmodule

module Switch (
  input  in_1,
  input  in_2,
  output out_3
);

  wire and_1_out, clock_1_out, nand_1_out, nand_2_out, nand_3_out, nand_4_out, nand_5_out, nand_6_out,
       nand_7_out, not_1_out, not_2_out, not_3_out;

  Clock clock_1 (.out(clock_1_out));
  not not_1 (not_1_out, in_1);
  not not_2 (not_2_out, nand_7_out);
  nand nand_1 (nand_1_out, nand_7_out, not_1_out, clock_1_out);
  nand nand_2 (nand_2_out, not_1_out, clock_1_out, not_2_out);
  nand nand_3 (nand_3_out, nand_1_out, nand_4_out);
  nand nand_4 (nand_4_out, nand_3_out, nand_2_out);
  not not_3 (not_3_out, nand_4_out);
  nand nand_5 (nand_5_out, clock_1_out, nand_4_out, in_1);
  nand nand_6 (nand_6_out, in_1, not_3_out, clock_1_out);
  and and_1 (and_1_out, in_2, out_3);
  nand nand_7 (nand_7_out, nand_5_out, and_1_out);
  nand nand_8 (out_3, nand_7_out, nand_6_out);
endmodule
