// Logisim project Question 2.circ as structural Verilog: 1 circuit, main circuit main
module main (
  input  V
);

  wire _74x01_2_out, _74x01_3_out, _74x01_4_out, _74x01_out, _74x08_out, _74x20_2_out, _74x20_3_out,
       _74x20_4_out, _74x20_out, button_1_out, clock_1_out, not_1_out, not_2_out, not_3_out;

  Button button_1 (.out(button_1_out));
  Clock clock_1 (.out(clock_1_out));
  not not_1 (not_1_out, button_1_out);
  not not_2 (not_2_out, _74x01_3_out);
  nand _74x20 (_74x20_out, _74x01_3_out, not_1_out, clock_1_out);
  nand _74x20_2 (_74x20_2_out, not_1_out, clock_1_out, not_2_out);
  nand _74x01 (_74x01_out, _74x20_out, _74x01_2_out);
  nand _74x01_2 (_74x01_2_out, _74x01_out, _74x20_2_out);
  not not_3 (not_3_out, _74x01_2_out);
  nand _74x20_3 (_74x20_3_out, clock_1_out, _74x01_2_out, button_1_out);
  nand _74x20_4 (_74x20_4_out, button_1_out, not_3_out, clock_1_out);
  and _74x08 (_74x08_out, V, _74x01_4_out);
  nand _74x01_3 (_74x01_3_out, _74x20_3_out, _74x08_out);
  nand _74x01_4 (_74x01_4_out, _74x01_3_out, _74x20_4_out);
  LED led_1 (.in(_74x01_4_out));

  // Notes on the sheet:
  //   74x04
  //   74x04
  //   1
  //   1
  //   2
  //   1
  //   74x04 - (SN74LS04)
  //   74x01 - (SN74LS01)
  //   74x20 - (SN74LS20)
  //   74x08 - (SN74LS08)
  //   74x04
  //   THIS ONE NEEDS TO BE SET AS 1 AFTER RESETTING TO 0
  //   V
endmodule
