// Logisim project Lab4 Question1.circ as structural Verilog: 1 circuit, main circuit main
module main (
  input  RIGHT,
  input  RIGHT_2,
  input  LEFT,
  input  LEFT_2,
  output o21,
  output o22,
  output o23,
  output o24,
  output o25,
  output o26,
  output o27,
  output o28,
  output o29,
  output o30,
  output out_15
);

  wire and_1_out, and_2_out, and_3_out, and_4_out, and_6_out, and_7_out, and_8_out, and_9_out, and_11_out,
       and_12_out, and_13_out, and_14_out, and_15_out, and_16_out, and_17_out, and_18_out, and_19_out,
       and_20_out, and_21_out, and_22_out, and_23_out, and_24_out, and_25_out, and_26_out, and_27_out,
       and_28_out, and_29_out, and_30_out, and_31_out, and_32_out, and_33_out, and_34_out, and_35_out,
       and_36_out, and_37_out, and_38_out, and_39_out, and_40_out, and_41_out, and_42_out, and_43_out,
       and_44_out, and_45_out, and_46_out, and_47_out, and_48_out, and_49_out, and_50_out, and_51_out,
       and_52_out, and_64_out, and_65_out, and_66_out, and_67_out, and_69_out, and_70_out, and_71_out,
       and_72_out, and_74_out, and_75_out, and_76_out, and_77_out, and_78_out, and_79_out, and_80_out,
       and_81_out, and_82_out, and_83_out, and_84_out, and_85_out, and_86_out, and_87_out, and_88_out,
       and_89_out, and_90_out, and_91_out, and_92_out, and_93_out, and_94_out, clock_1_out, clock_2_out,
       clock_3_out, clock_4_out, d_ff_1_q, d_ff_2_q, d_ff_3_q, d_ff_4_q, d_ff_5_q, d_ff_6_q, d_ff_7_q,
       d_ff_8_q, d_ff_9_q, d_ff_10_q, d_ff_11_q, d_ff_12_q, d_ff_13_q, d_ff_14_q, d_ff_15_q, d_ff_16_q,
       d_ff_17_q, d_ff_18_q, d_ff_19_q, d_ff_20_q, not_1_out, not_2_out, not_3_out, not_4_out, not_5_out,
       not_6_out, not_7_out, not_8_out, not_9_out, not_10_out, not_11_out, not_12_out, not_13_out,
       not_14_out, not_15_out, or_1_out, or_2_out, or_3_out, or_4_out, or_5_out, or_6_out, or_7_out,
       or_8_out, or_9_out, or_10_out, or_11_out, xnor_1_out, xnor_2_out, xnor_3_out, xnor_4_out, xor_1_out,
       xor_2_out, xor_3_out, xor_4_out, xor_5_out, xor_6_out, xor_7_out, xor_8_out, xor_9_out, xor_10_out,
       xor_11_out, xor_12_out, xor_13_out, xor_14_out, xor_15_out, xor_16_out, xor_17_out, xor_18_out,
       xor_19_out, xor_20_out;
  wire [4:0] or_12_out;
  wire [19:0] rom_1_data;

  and and_1 (and_1_out, RIGHT_2, d_ff_1_q);
  and and_2 (and_2_out, and_1_out, d_ff_2_q);
  and and_3 (and_3_out, and_2_out, d_ff_3_q);
  and and_4 (and_4_out, and_3_out, d_ff_4_q);
  // AND_Gate and_5 has open pins: in0=and_4_out, in1=d_ff_5_q, out=open
  and and_6 (and_6_out, LEFT_2, d_ff_6_q);
  and and_7 (and_7_out, and_6_out, d_ff_7_q);
  and and_8 (and_8_out, and_7_out, d_ff_8_q);
  and and_9 (and_9_out, and_8_out, d_ff_9_q);
  // AND_Gate and_10 has open pins: in0=and_9_out, in1=d_ff_10_q, out=open
  Clock clock_1 (.out(clock_1_out));
  Clock clock_2 (.out(clock_2_out));
  xor xor_1 (xor_1_out, d_ff_1_q, RIGHT_2);
  xor xor_2 (xor_2_out, d_ff_2_q, and_1_out);
  xor xor_3 (xor_3_out, d_ff_3_q, and_2_out);
  xor xor_4 (xor_4_out, d_ff_4_q, and_3_out);
  xor xor_5 (xor_5_out, d_ff_5_q, and_4_out);
  xor xor_6 (xor_6_out, d_ff_6_q, LEFT_2);
  xor xor_7 (xor_7_out, d_ff_7_q, and_6_out);
  xor xor_8 (xor_8_out, d_ff_8_q, and_7_out);
  xor xor_9 (xor_9_out, d_ff_9_q, and_8_out);
  xor xor_10 (xor_10_out, d_ff_10_q, and_9_out);
  D_Flip_Flop d_ff_1 (.clk(clock_2_out), .D(xor_1_out), .Q(d_ff_1_q), .reset(and_19_out));  // open: Qn, preset, en
  D_Flip_Flop d_ff_2 (.clk(clock_2_out), .D(xor_2_out), .Q(d_ff_2_q), .reset(and_19_out));  // open: Qn, preset, en
  D_Flip_Flop d_ff_3 (.clk(clock_2_out), .D(xor_3_out), .Q(d_ff_3_q), .reset(and_19_out));  // open: Qn, preset, en
  D_Flip_Flop d_ff_4 (.clk(clock_2_out), .D(xor_4_out), .Q(d_ff_4_q), .reset(and_19_out));  // open: Qn, preset, en
  D_Flip_Flop d_ff_5 (.clk(clock_2_out), .D(xor_5_out), .Q(d_ff_5_q), .reset(and_19_out));  // open: Qn, preset, en
  D_Flip_Flop d_ff_6 (
    .clk(clock_1_out), .D(xor_6_out), .Q(d_ff_6_q), .preset(or_1_out), .en(LEFT_2));  // open: Qn, reset
  or or_1 (or_1_out, and_26_out, and_20_out);
  D_Flip_Flop d_ff_7 (
    .clk(clock_1_out), .D(xor_7_out), .Q(d_ff_7_q), .preset(or_2_out), .en(LEFT_2));  // open: Qn, reset
  or or_2 (or_2_out, and_26_out, and_20_out);
  D_Flip_Flop d_ff_8 (
    .clk(clock_1_out), .D(xor_8_out), .Q(d_ff_8_q), .preset(and_26_out), .en(LEFT_2), .reset(and_20_out));  // open: Qn
  D_Flip_Flop d_ff_9 (
    .clk(clock_1_out), .D(xor_9_out), .Q(d_ff_9_q), .preset(or_3_out), .en(LEFT_2));  // open: Qn, reset
  or or_3 (or_3_out, and_26_out, and_20_out);
  D_Flip_Flop d_ff_10 (
    .clk(clock_1_out), .D(xor_10_out), .Q(d_ff_10_q), .preset(and_26_out), .en(LEFT_2), .reset(and_20_out));  // open: Qn
  and and_11 (and_11_out, d_ff_8_q, 1'b1);
  and and_12 (and_12_out, d_ff_10_q, 1'b1);
  and and_13 (and_13_out, d_ff_1_q, 1'b1);
  xnor xnor_1 (xnor_1_out, d_ff_2_q, 1'b0);
  and and_14 (and_14_out, d_ff_3_q, 1'b1);
  xnor xnor_2 (xnor_2_out, d_ff_4_q, 1'b0);
  and and_15 (and_15_out, d_ff_5_q, 1'b1);
  and and_16 (and_16_out, d_ff_6_q, 1'b1);
  and and_17 (and_17_out, d_ff_7_q, 1'b1);
  and and_18 (and_18_out, d_ff_9_q, 1'b1);
  and and_19 (and_19_out, and_13_out, xnor_1_out, and_14_out, xnor_2_out, and_15_out);
  not not_1 (not_1_out, d_ff_6_q);
  not not_2 (not_2_out, d_ff_7_q);
  not not_3 (not_3_out, d_ff_8_q);
  and and_20 (and_20_out, and_16_out, and_17_out, and_11_out, and_18_out, and_12_out);
  not not_4 (not_4_out, d_ff_9_q);
  not not_5 (not_5_out, d_ff_10_q);
  and and_21 (and_21_out, RIGHT_2, d_ff_1_q);
  and and_22 (and_22_out, RIGHT_2, d_ff_2_q);
  and and_23 (and_23_out, RIGHT_2, d_ff_3_q);
  and and_24 (and_24_out, RIGHT_2, d_ff_4_q);
  and and_25 (and_25_out, RIGHT_2, d_ff_5_q);
  and and_26 (and_26_out, not_5_out, not_4_out, not_3_out, not_2_out, not_1_out);
  and and_27 (and_27_out, LEFT_2, not_1_out);
  and and_28 (and_28_out, not_2_out, LEFT_2);
  and and_29 (and_29_out, not_3_out, LEFT_2);
  and and_30 (and_30_out, LEFT_2, not_4_out);
  and and_31 (and_31_out, LEFT_2, not_5_out);
  or or_4 (or_4_out, and_27_out, and_21_out);
  or or_5 (or_5_out, and_28_out, and_22_out);
  not not_6 (not_6_out, or_4_out);
  or or_6 (or_6_out, and_29_out, and_23_out);
  not not_7 (not_7_out, or_5_out);
  or or_7 (or_7_out, and_30_out, and_24_out);
  not not_8 (not_8_out, or_7_out);
  not not_9 (not_9_out, or_6_out);
  or or_8 (or_8_out, and_31_out, and_25_out);
  not not_10 (not_10_out, or_8_out);
  and and_32 (and_32_out, not_8_out, not_9_out, not_7_out, not_6_out, not_10_out);
  and and_33 (and_33_out, not_10_out, not_8_out, not_9_out, not_7_out, or_4_out);
  and and_34 (and_34_out, not_10_out, not_8_out, not_9_out, or_5_out, not_6_out);
  and and_35 (and_35_out, not_10_out, not_8_out, not_9_out, or_5_out, or_4_out);
  and and_36 (and_36_out, not_6_out, not_7_out, or_6_out, not_8_out, not_10_out);
  and and_37 (and_37_out, not_10_out, not_8_out, or_6_out, not_7_out, or_4_out);
  and and_38 (and_38_out, not_6_out, or_5_out, or_6_out, not_8_out, not_10_out);
  and and_39 (and_39_out, not_10_out, not_8_out, or_6_out, or_5_out, or_4_out);
  and and_40 (and_40_out, not_10_out, or_7_out, not_9_out, not_7_out, not_6_out);
  and and_41 (and_41_out, not_10_out, or_7_out, not_9_out, not_7_out, or_4_out);
  and and_42 (and_42_out, not_10_out, or_7_out, not_9_out, or_5_out, not_6_out);
  and and_43 (and_43_out, not_10_out, or_7_out, not_9_out, or_5_out, or_4_out);
  and and_44 (and_44_out, not_10_out, or_7_out, or_6_out, not_7_out, not_6_out);
  and and_45 (and_45_out, not_10_out, or_7_out, or_6_out, not_7_out, or_4_out);
  and and_46 (and_46_out, not_10_out, or_7_out, or_6_out, or_5_out, not_6_out);
  and and_47 (and_47_out, not_10_out, or_7_out, or_6_out, or_5_out, or_4_out);
  and and_48 (and_48_out, or_8_out, not_8_out, not_9_out, not_7_out, not_6_out);
  and and_49 (and_49_out, or_8_out, not_8_out, not_9_out, not_7_out, or_4_out);
  and and_50 (and_50_out, or_8_out, not_8_out, not_9_out, or_5_out, not_6_out);
  and and_51 (and_51_out, or_8_out, not_8_out, not_9_out, or_5_out, or_4_out);
  and and_52 (and_52_out, or_8_out, not_8_out, or_6_out, not_7_out, not_6_out);
  and and_53 (o21, or_8_out, not_8_out, or_6_out, not_7_out, or_4_out);
  and and_54 (o22, or_8_out, not_8_out, or_6_out, or_5_out, not_6_out);
  and and_55 (o23, or_8_out, not_8_out, or_6_out, or_5_out, or_4_out);
  and and_56 (o24, or_8_out, or_7_out, not_9_out, not_7_out, not_6_out);
  and and_57 (o25, or_8_out, or_7_out, not_9_out, not_7_out, or_4_out);
  and and_58 (o26, or_8_out, or_7_out, not_9_out, or_5_out, not_6_out);
  and and_59 (o27, or_8_out, or_7_out, not_9_out, or_5_out, or_4_out);
  and and_60 (o28, or_8_out, or_7_out, or_6_out, not_7_out, not_6_out);
  and and_61 (o29, or_8_out, or_7_out, or_6_out, not_7_out, or_4_out);
  and and_62 (o30, or_8_out, or_7_out, or_6_out, or_5_out, not_6_out);
  and and_63 (out_15, or_8_out, or_7_out, or_6_out, or_5_out, or_4_out);
  LED led_1 (.in(and_33_out));
  LED led_2 (.in(and_36_out));
  LED led_3 (.in(and_35_out));
  LED led_4 (.in(and_34_out));
  LED led_5 (.in(and_37_out));
  LED led_6 (.in(and_39_out));
  LED led_7 (.in(and_40_out));
  LED led_8 (.in(and_38_out));
  LED led_9 (.in(and_41_out));
  LED led_10 (.in(and_42_out));
  LED led_11 (.in(and_44_out));
  LED led_12 (.in(and_43_out));
  LED led_13 (.in(and_48_out));
  LED led_14 (.in(and_45_out));
  LED led_15 (.in(and_46_out));
  LED led_16 (.in(and_47_out));
  LED led_17 (.in(and_51_out));
  LED led_18 (.in(and_50_out));
  LED led_19 (.in(and_49_out));
  LED led_20 (.in(and_52_out));
  and and_64 (and_64_out, LEFT, d_ff_11_q);
  and and_65 (and_65_out, and_64_out, d_ff_12_q);
  and and_66 (and_66_out, and_65_out, d_ff_13_q);
  and and_67 (and_67_out, and_66_out, d_ff_14_q);
  // AND_Gate and_68 has open pins: in0=and_67_out, in1=d_ff_15_q, out=open
  and and_69 (and_69_out, RIGHT, d_ff_16_q);
  and and_70 (and_70_out, and_69_out, d_ff_17_q);
  and and_71 (and_71_out, and_70_out, d_ff_18_q);
  and and_72 (and_72_out, and_71_out, d_ff_19_q);
  // AND_Gate and_73 has open pins: in0=and_72_out, in1=d_ff_20_q, out=open
  Clock clock_3 (.out(clock_3_out));
  xor xor_11 (xor_11_out, d_ff_16_q, RIGHT);
  xor xor_12 (xor_12_out, d_ff_17_q, and_69_out);
  xor xor_13 (xor_13_out, d_ff_18_q, and_70_out);
  xor xor_14 (xor_14_out, d_ff_19_q, and_71_out);
  xor xor_15 (xor_15_out, d_ff_20_q, and_72_out);
  Clock clock_4 (.out(clock_4_out));
  xor xor_16 (xor_16_out, d_ff_11_q, LEFT);
  xor xor_17 (xor_17_out, d_ff_12_q, and_64_out);
  xor xor_18 (xor_18_out, d_ff_13_q, and_65_out);
  xor xor_19 (xor_19_out, d_ff_14_q, and_66_out);
  xor xor_20 (xor_20_out, d_ff_15_q, and_67_out);
  D_Flip_Flop d_ff_11 (
    .clk(clock_4_out), .D(xor_16_out), .Q(d_ff_11_q), .preset(or_9_out), .en(LEFT));  // open: Qn, reset
  or or_9 (or_9_out, and_89_out, and_83_out);
  D_Flip_Flop d_ff_12 (
    .clk(clock_4_out), .D(xor_17_out), .Q(d_ff_12_q), .preset(or_10_out), .en(LEFT));  // open: Qn, reset
  or or_10 (or_10_out, and_89_out, and_83_out);
  D_Flip_Flop d_ff_13 (
    .clk(clock_4_out), .D(xor_18_out), .Q(d_ff_13_q), .preset(and_89_out), .en(LEFT), .reset(and_83_out));  // open: Qn
  D_Flip_Flop d_ff_14 (
    .clk(clock_4_out), .D(xor_19_out), .Q(d_ff_14_q), .preset(or_11_out), .en(LEFT));  // open: Qn, reset
  or or_11 (or_11_out, and_89_out, and_83_out);
  D_Flip_Flop d_ff_15 (
    .clk(clock_4_out), .D(xor_20_out), .Q(d_ff_15_q), .preset(and_89_out), .en(LEFT), .reset(and_83_out));  // open: Qn
  D_Flip_Flop d_ff_16 (.clk(clock_3_out), .D(xor_11_out), .Q(d_ff_16_q), .reset(and_82_out));  // open: Qn, preset, en
  D_Flip_Flop d_ff_17 (.clk(clock_3_out), .D(xor_12_out), .Q(d_ff_17_q), .reset(and_82_out));  // open: Qn, preset, en
  D_Flip_Flop d_ff_18 (.clk(clock_3_out), .D(xor_13_out), .Q(d_ff_18_q), .reset(and_82_out));  // open: Qn, preset, en
  D_Flip_Flop d_ff_19 (.clk(clock_3_out), .D(xor_14_out), .Q(d_ff_19_q), .reset(and_82_out));  // open: Qn, preset, en
  D_Flip_Flop d_ff_20 (.clk(clock_3_out), .D(xor_15_out), .Q(d_ff_20_q), .reset(and_82_out));  // open: Qn, preset, en
  and and_74 (and_74_out, d_ff_16_q, 1'b1);
  xnor xnor_3 (xnor_3_out, d_ff_17_q, 1'b0);
  and and_75 (and_75_out, d_ff_18_q, 1'b1);
  xnor xnor_4 (xnor_4_out, d_ff_19_q, 1'b0);
  and and_76 (and_76_out, d_ff_20_q, 1'b1);
  and and_77 (and_77_out, d_ff_11_q, 1'b1);
  and and_78 (and_78_out, d_ff_12_q, 1'b1);
  and and_79 (and_79_out, d_ff_13_q, 1'b1);
  and and_80 (and_80_out, d_ff_14_q, 1'b1);
  and and_81 (and_81_out, d_ff_15_q, 1'b1);
  and and_82 (and_82_out, and_74_out, xnor_3_out, and_75_out, xnor_4_out, and_76_out);
  not not_11 (not_11_out, d_ff_11_q);
  not not_12 (not_12_out, d_ff_12_q);
  not not_13 (not_13_out, d_ff_13_q);
  and and_83 (and_83_out, and_77_out, and_78_out, and_79_out, and_80_out, and_81_out);
  not not_14 (not_14_out, d_ff_14_q);
  not not_15 (not_15_out, d_ff_15_q);
  and and_84 (and_84_out, RIGHT, d_ff_16_q);
  and and_85 (and_85_out, RIGHT, d_ff_17_q);
  and and_86 (and_86_out, RIGHT, d_ff_18_q);
  and and_87 (and_87_out, RIGHT, d_ff_19_q);
  and and_88 (and_88_out, RIGHT, d_ff_20_q);
  and and_89 (and_89_out, not_15_out, not_14_out, not_13_out, not_12_out, not_11_out);
  and and_90 (and_90_out, LEFT, not_11_out);
  and and_91 (and_91_out, not_12_out, LEFT);
  and and_92 (and_92_out, not_13_out, LEFT);
  and and_93 (and_93_out, LEFT, not_14_out);
  and and_94 (and_94_out, LEFT, not_15_out);
  or or_12 (or_12_out[0], and_90_out, and_84_out);
  or or_13 (or_12_out[1], and_91_out, and_85_out);
  or or_14 (or_12_out[2], and_92_out, and_86_out);
  LED led_21 (.in(rom_1_data[19]));
  or or_15 (or_12_out[3], and_93_out, and_87_out);
  ROM #(.addrWidth(5), .dataWidth(20)) rom_1 (.addr(or_12_out), .data(rom_1_data));  // open: sel
  LED led_22 (.in(rom_1_data[17]));
  LED led_23 (.in(rom_1_data[18]));
  LED led_24 (.in(rom_1_data[16]));
  LED led_25 (.in(rom_1_data[15]));
  or or_16 (or_12_out[4], and_94_out, and_88_out);
  LED led_26 (.in(rom_1_data[11]));
  LED led_27 (.in(rom_1_data[12]));
  LED led_28 (.in(rom_1_data[13]));
  LED led_29 (.in(rom_1_data[14]));
  LED led_30 (.in(rom_1_data[9]));
  LED led_31 (.in(rom_1_data[10]));
  LED led_32 (.in(rom_1_data[8]));
  LED led_33 (.in(rom_1_data[7]));
  LED led_34 (.in(rom_1_data[6]));
  LED led_35 (.in(rom_1_data[5]));
  LED led_36 (.in(rom_1_data[4]));
  LED led_37 (.in(rom_1_data[3]));
  LED led_38 (.in(rom_1_data[1]));
  LED led_39 (.in(rom_1_data[0]));
  LED led_40 (.in(rom_1_data[2]));

  // Notes on the sheet:
  //   d0
  //   d2
  //   d1
  //   o2
  //   o3
  //   o4
  //   o5
  //   o6
  //   o7
  //   o8
  //   o9
  //   o10
  //   o11
  //   o12
  //   o13
  //   o14
  //   o15
  //   o16
  //   o17
  //   o18
  //   o19
  //   o20
  //   contents of rom_1 (hex, n*v repeats v):
  //   0 80000 40000 20000 10000 8000 4000 2000 1000 800 400 200 100 80 40 20 10 8 4 2 1
endmodule
