// Logisim project Lab4 Question2.circ as structural Verilog: 6 circuits, main circuit main
module main (
  input  From_ROM,
  input  To_RAM,
  input  From_RAM,
  input  To_Display,
  input  From_Display,
  input  To_Data_Bus,
  input  From_Data_Bus,
  input  [7:0] Data,
  input  From_Data,
  input  [7:0] ROM_Address,
  input  [7:0] RAM_Address
);

  wire bus_stuff_1_enable, clock_1_out, RAM_STUFF_en, RAM_STUFF_ld, RAM_STUFF_store, register_1_q,
       register_2_q, register_3_q, register_4_q, register_5_q, register_6_q, register_7_q, register_9_q;
  wire [3:0] pin_convert_3_out_11, pin_convert_3_out_11_2;
  wire [7:0] DATA_BUS_q, pin_convert_1_out_11, pin_convert_2_out_11, ram_1_data, register_8_q, register_10_q,
       register_11_q, rom_1_data;

  Register #(.width(1)) register_1 (.D(From_ROM), .en(1'b1), .Q(register_1_q), .clk(clock_1_out));  // open: clr
  Register #(.width(1)) register_2 (.D(To_RAM), .en(1'b1), .Q(register_2_q), .clk(clock_1_out));  // open: clr
  Register #(.width(1)) register_3 (.D(From_RAM), .en(1'b1), .Q(register_3_q), .clk(clock_1_out));  // open: clr
  Register #(.width(1)) register_4 (.D(To_Display), .en(1'b1), .Q(register_4_q), .clk(clock_1_out));  // open: clr
  Register #(.width(1)) register_5 (.D(From_Display), .en(1'b1), .Q(register_5_q), .clk(clock_1_out));  // open: clr
  Register #(.width(1)) register_6 (.D(To_Data_Bus), .en(1'b1), .Q(register_6_q), .clk(clock_1_out));  // open: clr
  Register #(.width(1)) register_7 (.D(From_Data_Bus), .en(1'b1), .Q(register_7_q), .clk(clock_1_out));  // open: clr
  Register register_8 (.D(Data), .en(1'b1), .Q(register_8_q), .clk(clock_1_out));  // open: clr
  Register #(.width(1)) register_9 (.D(From_Data), .en(1'b1), .Q(register_9_q), .clk(clock_1_out));  // open: clr
  Register register_10 (.D(ROM_Address), .en(1'b1), .Q(register_10_q), .clk(clock_1_out));  // open: clr
  Register register_11 (.D(RAM_Address), .en(1'b1), .Q(register_11_q), .clk(clock_1_out));  // open: clr
  Clock clock_1 (.out(clock_1_out));
  ROM rom_1 (.addr(register_10_q), .data(rom_1_data), .sel(register_1_q));
  Pin_Convert pin_convert_1 (
    .To(register_2_q), .Current_Value(ram_1_data), .FROM_0(register_1_q), .FROM_1(register_5_q),
    .FROM_2(register_7_q), .FROM_3(register_9_q), .VAL_OF_0(rom_1_data),
    .VAL_OF_1({pin_convert_3_out_11, pin_convert_3_out_11_2}), .VAL_OF_2(DATA_BUS_q),
    .VAL_OF_3(register_8_q), .out_11(pin_convert_1_out_11));
  RAM_Stuff RAM_STUFF (
    .Read(register_3_q), .Write(register_2_q), .Store(RAM_STUFF_store), .Ld(RAM_STUFF_ld), .En(RAM_STUFF_en));
  RAM #(.bus("separate")) ram_1 (
    .addr(register_11_q), .din(pin_convert_1_out_11), .data(ram_1_data), .str(RAM_STUFF_store),
    .sel(RAM_STUFF_en), .clk(clock_1_out), .ld(RAM_STUFF_ld));  // open: clr
  Pin_Convert pin_convert_2 (
    .To(register_6_q), .Current_Value(DATA_BUS_q), .FROM_0(register_1_q), .FROM_1(register_3_q),
    .FROM_2(register_5_q), .FROM_3(register_9_q), .VAL_OF_0(rom_1_data), .VAL_OF_1(ram_1_data),
    .VAL_OF_2({pin_convert_3_out_11, pin_convert_3_out_11_2}), .VAL_OF_3(register_8_q),
    .out_11(pin_convert_2_out_11));
  Register #(.trigger("high")) DATA_BUS (
    .D(pin_convert_2_out_11), .Q(DATA_BUS_q), .clk(bus_stuff_1_enable));  // open: en, clr
  Bus_Stuff bus_stuff_1 (.Read(register_7_q), .Write(register_6_q), .Enable(bus_stuff_1_enable));
  Pin_Convert pin_convert_3 (
    .To(register_4_q), .Current_Value({pin_convert_3_out_11, pin_convert_3_out_11_2}), .FROM_0(register_1_q),
    .FROM_1(register_3_q), .FROM_2(register_7_q), .FROM_3(register_9_q), .VAL_OF_0(rom_1_data),
    .VAL_OF_1(ram_1_data), .VAL_OF_2(DATA_BUS_q), .VAL_OF_3(register_8_q),
    .out_11({pin_convert_3_out_11, pin_convert_3_out_11_2}));
  Hex_Digit_Display hex_digit_display_1 (.value(pin_convert_3_out_11));  // open: dp
  Hex_Digit_Display hex_digit_display_2 (.value(pin_convert_3_out_11_2));  // open: dp

  // Notes on the sheet:
  //   ROM
  //   contents of rom_1 (hex, n*v repeats v):
  //   0 1 2 3 4 5 6 7 8 9 a b c d e f
  //   RAM
endmodule

module Mux_Stuff (
  input  To,
  input  FROM_0,
  input  FROM_1,
  input  FROM_2,
  input  FROM_3,
  output [2:0] Pins
);

  wire or_1_out, or_2_out, xor_1_out;

  or or_1 (or_1_out, FROM_2, FROM_0);
  ExactlyOne xor_1 (.out(xor_1_out), .in0(FROM_0), .in1(FROM_1), .in2(FROM_2), .in3(FROM_3));
  or or_2 (or_2_out, FROM_2, FROM_1);
  and and_1 (Pins[0], To, xor_1_out, or_1_out);
  and and_2 (Pins[1], xor_1_out, or_2_out, To);
  and and_3 (Pins[2], xor_1_out, To, FROM_3);
endmodule

module RAM_Stuff (
  input  Read,
  input  Write,
  output Store,
  output Ld,
  output En
);

  not not_1 (Ld, Write);
  or or_1 (En, Read, Write);

  assign Store = Write;
endmodule

// PIN STUFF
module Pin_Convert (
  input  To,
  input  [7:0] Current_Value,
  input  FROM_0,
  input  FROM_1,
  input  FROM_2,
  input  FROM_3,
  input  [7:0] VAL_OF_0,
  input  [7:0] VAL_OF_1,
  input  [7:0] VAL_OF_2,
  input  [7:0] VAL_OF_3,
  output [7:0] out_11
);

  wire [2:0] MUX_STUFF_pins;

  Mux_Stuff MUX_STUFF (
    .To(To), .FROM_0(FROM_0), .FROM_1(FROM_1), .FROM_2(FROM_2), .FROM_3(FROM_3), .Pins(MUX_STUFF_pins));
  Multiplexer #(.select(3), .width(8), .disabled(0), .enable("false")) multiplexer_1 (
    .in0(Current_Value), .in1(VAL_OF_0), .in2(VAL_OF_1), .in3(VAL_OF_2), .in4(VAL_OF_3), .out(out_11),
    .sel(MUX_STUFF_pins));  // open: in5, in6, in7

  // Notes on the sheet:
  //   THIS PART DECIPHERS WHAT TO VALUE TO PUT INTO WHICH OBJECT
  //   000 MAINTAIN
  //   001 VAL OF 0
  //   010 VAL OF 1
  //   011 VAL OF 2
  //   100 VAL OF 3
endmodule

module Bus_Stuff (
  input  Read,
  input  Write,
  output Enable
);

  or or_1 (Enable, Read, Write);
endmodule

module Display_Stuff (
  input  To_this_component,
  input  [7:0] Current_Value,
  input  From_source__0,
  input  From_source__1,
  input  From_source__2,
  input  From_source__3,
  input  [7:0] Value_source_0,
  input  [7:0] Value_source_1,
  input  [7:0] Value_source_2,
  input  [7:0] Value_source_3,
  output [7:0] out_11
);

  wire [2:0] mux_stuff_1_pins;

  Mux_Stuff mux_stuff_1 (
    .To(To_this_component), .FROM_0(From_source__0), .FROM_1(From_source__1), .FROM_2(From_source__2),
    .FROM_3(From_source__3), .Pins(mux_stuff_1_pins));
  Multiplexer #(.select(3), .width(8), .disabled(0), .enable("false")) multiplexer_1 (
    .in0(Current_Value), .in1(Value_source_0), .in2(Value_source_1), .in3(Value_source_2),
    .in4(Value_source_3), .out(out_11), .sel(mux_stuff_1_pins));  // open: in5, in6, in7

  // Notes on the sheet:
  //   000: Maintain, 001: Source 0, etc.
endmodule
