// Logisim project Lab4 Question3.circ as structural Verilog: 4 circuits, main circuit main
module main (
  input  a7,
  input  a6,
  input  a5,
  input  a4,
  input  a3,
  input  a2,
  input  a1,
  input  a0,
  input  cin,
  input  a7_2,
  input  a6_2,
  input  a5_2,
  input  a4_2,
  input  a3_2,
  input  a2_2,
  input  a1_2,
  input  a0_2,
  input  b7,
  input  b6,
  input  b5,
  input  b4,
  input  b3,
  input  b2,
  input  b1,
  input  b0,
  input  b7_2,
  input  b6_2,
  input  b5_2,
  input  b4_2,
  input  b3_2,
  input  b2_2,
  input  b1_2,
  input  b0_2,
  input  in_34,
  input  in_35,
  input  in_36,
  input  in_37,
  input  in_38,
  input  in_39,
  input  in_40,
  input  in_41,
  input  in_42,
  input  in_43,
  input  in_44,
  input  UPDATE,
  input  SUB,
  input  a7_3,
  input  a6_3,
  input  a5_3,
  input  a4_3,
  input  a3_3,
  input  a2_3,
  input  a1_3,
  input  a0_3,
  input  b7_3,
  input  b6_3,
  input  b5_3,
  input  b4_3,
  input  b3_3,
  input  b2_3,
  input  b1_3,
  input  b0_3,
  output o7,
  output o6,
  output o5,
  output o4,
  output o3,
  output o2,
  output o1,
  output o0,
  output out_71,
  output out_72,
  output out_73,
  output out_74,
  output out_75,
  output out_76,
  output out_77,
  output out_78,
  output out_79,
  output out_80,
  output out_81,
  output o7_2,
  output o6_2,
  output o5_2,
  output o4_2,
  output o3_2,
  output o2_2,
  output o1_2,
  output o0_2
);

  wire and_1_out, clock_1_out, comparator_1_out_6, comparator_1_out_7, comparator_1_out_8,
       comparator_2_out_6, comparator_2_out_7, comparator_2_out_8, comparator_3_out_6, comparator_3_out_7,
       comparator_3_out_8, comparator_4_out_6, comparator_4_out_7, comparator_4_out_8, comparator_5_out_6,
       comparator_5_out_7, comparator_5_out_8, comparator_6_out_6, comparator_6_out_7, comparator_6_out_8,
       coparator_begin_1_out_3, coparator_begin_1_out_4, coparator_begin_1_out_5, FA_2_out_5, FA_3_out_5,
       FA_4_out_5, FA_5_out_5, FA_6_out_5, FA_7_out_5, FA_8_out_5, FA_9_out_5, FA_10_out_5, FA_11_out_5,
       FA_12_out_5, FA_13_out_5, FA_14_out_5, FA_15_out_5, FA_16_out_5, FA_out_5, multiplexer_1_out,
       multiplexer_2_out, multiplexer_3_out, multiplexer_4_out, multiplexer_5_out, multiplexer_6_out,
       multiplexer_7_out, multiplexer_8_out, xor_1_out, xor_2_out, xor_3_out, xor_4_out, xor_5_out,
       xor_6_out, xor_7_out, xor_8_out, xor_9_out;

  xor xor_1 (xor_1_out, 1'b0, SUB);
  xor xor_2 (xor_2_out, SUB, b0_3);
  xor xor_3 (xor_3_out, SUB, b1_3);
  xor xor_4 (xor_4_out, SUB, b2_3);
  xor xor_5 (xor_5_out, SUB, b3_3);
  xor xor_6 (xor_6_out, SUB, b4_3);
  xor xor_7 (xor_7_out, SUB, b5_3);
  xor xor_8 (xor_8_out, SUB, b6_3);
  xor xor_9 (xor_9_out, SUB, b7_3);
  FULLADDER FA (.a(a0_2), .b(b0_2), .ci(cin), .out_4(o0), .out_5(FA_out_5));
  FULLADDER FA_2 (.a(a1_2), .b(b1_2), .ci(FA_out_5), .out_4(o1), .out_5(FA_2_out_5));
  FULLADDER FA_3 (.a(a2_2), .b(b2_2), .ci(FA_2_out_5), .out_4(o2), .out_5(FA_3_out_5));
  FULLADDER FA_4 (.a(b3_2), .b(a3_2), .ci(FA_3_out_5), .out_4(o3), .out_5(FA_4_out_5));
  FULLADDER FA_5 (.a(a4_2), .b(b4_2), .ci(FA_4_out_5), .out_4(o4), .out_5(FA_5_out_5));
  FULLADDER FA_6 (.a(b5_2), .b(a5_2), .ci(FA_5_out_5), .out_4(o5), .out_5(FA_6_out_5));
  FULLADDER FA_7 (.a(b6_2), .b(a6_2), .ci(FA_6_out_5), .out_4(o6), .out_5(FA_7_out_5));
  FULLADDER FA_8 (.a(b7_2), .b(a7_2), .ci(FA_7_out_5), .out_4(o7), .out_5(FA_8_out_5));
  FULLADDER FA_9 (.a(xor_2_out), .b(a0_3), .ci(xor_1_out), .out_4(o0_2), .out_5(FA_9_out_5));
  FULLADDER FA_10 (.a(xor_3_out), .b(a1_3), .ci(FA_9_out_5), .out_4(o1_2), .out_5(FA_10_out_5));
  FULLADDER FA_11 (.a(xor_4_out), .b(a2_3), .ci(FA_10_out_5), .out_4(o2_2), .out_5(FA_11_out_5));
  FULLADDER FA_12 (.a(xor_5_out), .b(a3_3), .ci(FA_11_out_5), .out_4(o3_2), .out_5(FA_12_out_5));
  FULLADDER FA_13 (.a(xor_6_out), .b(a4_3), .ci(FA_12_out_5), .out_4(o4_2), .out_5(FA_13_out_5));
  FULLADDER FA_14 (.a(xor_7_out), .b(a5_3), .ci(FA_13_out_5), .out_4(o5_2), .out_5(FA_14_out_5));
  FULLADDER FA_15 (.a(xor_8_out), .b(a6_3), .ci(FA_14_out_5), .out_4(o6_2), .out_5(FA_15_out_5));
  FULLADDER FA_16 (.a(xor_9_out), .b(a7_3), .ci(FA_15_out_5), .out_4(o7_2), .out_5(FA_16_out_5));
  Clock clock_1 (.out(clock_1_out));
  Multiplexer #(.select(3), .enable("false")) multiplexer_1 (
    .in0(out_74), .in1(in_34), .in2(out_75), .in3(out_76), .in4(out_78), .in5(in_34), .in6(in_34),
    .in7(in_34), .out(multiplexer_1_out), .sel({in_42, in_43, in_44}));
  Register #(.width(1)) register_1 (.D(multiplexer_1_out), .Q(out_74), .clk(and_1_out));  // open: en, clr
  and and_1 (and_1_out, UPDATE, clock_1_out);
  Coparator_Begin coparator_begin_1 (
    .BIT(a7), .BIT_2(b7), .out_3(coparator_begin_1_out_3), .out_4(coparator_begin_1_out_4),
    .out_5(coparator_begin_1_out_5));
  Multiplexer #(.select(3), .enable("false")) multiplexer_2 (
    .in0(out_75), .in1(in_35), .in2(out_76), .in3(out_77), .in4(out_79), .in5(out_74), .in6(in_35),
    .in7(in_35), .out(multiplexer_2_out), .sel({in_42, in_43, in_44}));
  Comparator comparator_1 (
    .BIT(a6), .BIT_2(b6), .G(coparator_begin_1_out_3), .E(coparator_begin_1_out_4),
    .L(coparator_begin_1_out_5), .out_6(comparator_1_out_6), .out_7(comparator_1_out_7),
    .out_8(comparator_1_out_8));
  Register #(.width(1)) register_2 (.D(multiplexer_2_out), .Q(out_75), .clk(and_1_out));  // open: en, clr
  Comparator comparator_2 (
    .BIT(a5), .BIT_2(b5), .G(comparator_1_out_6), .E(comparator_1_out_7), .L(comparator_1_out_8),
    .out_6(comparator_2_out_6), .out_7(comparator_2_out_7), .out_8(comparator_2_out_8));
  Multiplexer #(.select(3)) multiplexer_3 (
    .in0(out_76), .in1(in_36), .in2(out_77), .in3(out_78), .in4(out_80), .in5(out_75), .in6(out_74),
    .in7(in_36), .out(multiplexer_3_out), .sel({in_42, in_43, in_44}));  // open: en
  Comparator comparator_3 (
    .BIT(a4), .BIT_2(b4), .G(comparator_2_out_6), .E(comparator_2_out_7), .L(comparator_2_out_8),
    .out_6(comparator_3_out_6), .out_7(comparator_3_out_7), .out_8(comparator_3_out_8));
  Register #(.width(1)) register_3 (.D(multiplexer_3_out), .Q(out_76), .clk(and_1_out));  // open: en, clr
  Comparator comparator_4 (
    .BIT(a3), .BIT_2(b3), .G(comparator_3_out_6), .E(comparator_3_out_7), .L(comparator_3_out_8),
    .out_6(comparator_4_out_6), .out_7(comparator_4_out_7), .out_8(comparator_4_out_8));
  Multiplexer #(.select(3)) multiplexer_4 (
    .in0(out_77), .in1(in_37), .in2(out_78), .in3(out_79), .in4(out_81), .in5(out_76), .in6(out_75),
    .in7(in_37), .out(multiplexer_4_out), .sel({in_42, in_43, in_44}));  // open: en
  Register #(.width(1)) register_4 (.D(multiplexer_4_out), .Q(out_77), .clk(and_1_out));  // open: en, clr
  Comparator comparator_5 (
    .BIT(a2), .BIT_2(b2), .G(comparator_4_out_6), .E(comparator_4_out_7), .L(comparator_4_out_8),
    .out_6(comparator_5_out_6), .out_7(comparator_5_out_7), .out_8(comparator_5_out_8));
  Multiplexer #(.select(3)) multiplexer_5 (
    .in0(out_78), .in1(in_38), .in2(out_79), .in3(out_80), .in4(in_38), .in5(out_77), .in6(out_76),
    .in7(out_74), .out(multiplexer_5_out), .sel({in_42, in_43, in_44}));  // open: en
  Comparator comparator_6 (
    .BIT(a1), .BIT_2(b1), .G(comparator_5_out_6), .E(comparator_5_out_7), .L(comparator_5_out_8),
    .out_6(comparator_6_out_6), .out_7(comparator_6_out_7), .out_8(comparator_6_out_8));
  Register #(.width(1)) register_5 (.D(multiplexer_5_out), .Q(out_78), .clk(and_1_out));  // open: en, clr
  Comparator comparator_7 (
    .BIT(a0), .BIT_2(b0), .G(comparator_6_out_6), .E(comparator_6_out_7), .L(comparator_6_out_8),
    .out_6(out_71), .out_7(out_72), .out_8(out_73));
  Multiplexer #(.select(3)) multiplexer_6 (
    .in0(out_79), .in1(in_39), .in2(out_80), .in3(out_81), .in4(in_39), .in5(out_78), .in6(out_77),
    .in7(out_75), .out(multiplexer_6_out), .sel({in_42, in_43, in_44}));  // open: en
  Register #(.width(1)) register_6 (.D(multiplexer_6_out), .Q(out_79), .clk(and_1_out));  // open: en, clr
  Multiplexer #(.select(3)) multiplexer_7 (
    .in0(out_80), .in1(in_40), .in2(out_81), .in3(in_40), .in4(in_40), .in5(out_79), .in6(out_78),
    .in7(out_76), .out(multiplexer_7_out), .sel({in_42, in_43, in_44}));  // open: en
  Register #(.width(1)) register_7 (.D(multiplexer_7_out), .Q(out_80), .clk(and_1_out));  // open: en, clr
  Multiplexer #(.select(3)) multiplexer_8 (
    .in0(out_81), .in1(in_41), .in2(in_41), .in3(in_41), .in4(in_41), .in5(out_80), .in6(out_79),
    .in7(out_77), .out(multiplexer_8_out), .sel({in_42, in_43, in_44}));  // open: en
  Register #(.width(1)) register_8 (.D(multiplexer_8_out), .Q(out_81), .clk(and_1_out));  // open: en, clr

  // Notes on the sheet:
  //   8 BIT FULL  ADDERS
  //   8 BIT FULL ADDER AND SUBTRACTOR (WHEN SUB IS 1)
  //   c0
  //   s
  //   000 Maintain
  //   001 Load
  //   011 Shift Left 2
  //   100 Shift Left 4
  //   101 Shift Right 1
  //   110 Shift Right 2
  //   111 Shift Right 4
  //   010 Shift Left 1
  //   8 BIT MAGNITUDE COMPARATOR
  //   LEFT  AND RIGHT BARREL SHIFTER
endmodule

module FULLADDER (
  input  a,
  input  b,
  input  ci,
  output out_4,
  output out_5
);

  wire and_1_out, and_2_out, xor_1_out;

  xor xor_1 (xor_1_out, a, b);
  and and_1 (and_1_out, ci, xor_1_out);
  and and_2 (and_2_out, b, a);
  xor xor_2 (out_4, ci, xor_1_out);
  or or_1 (out_5, and_1_out, and_1_out, and_2_out);
endmodule

module Comparator (
  input  BIT,
  input  BIT_2,
  input  G,
  input  E,
  input  L,
  output out_6,
  output out_7,
  output out_8
);

  wire and_1_out, and_2_out, and_3_out, and_4_out, not_1_out, not_2_out, not_3_out, not_4_out, or_1_out,
       or_2_out, xnor_1_out;

  and and_1 (and_1_out, G, 1'b1);
  and and_2 (and_2_out, L, 1'b1);
  not not_1 (not_1_out, BIT_2);
  not not_2 (not_2_out, BIT);
  and and_3 (and_3_out, BIT, not_1_out);
  xnor xnor_1 (xnor_1_out, BIT, BIT_2);
  and and_4 (and_4_out, not_2_out, BIT_2);
  or or_1 (or_1_out, and_3_out, and_1_out);
  and and_5 (out_7, xnor_1_out, E);
  not not_3 (not_3_out, and_1_out);
  or or_2 (or_2_out, and_4_out, and_2_out);
  not not_4 (not_4_out, and_2_out);
  and and_6 (out_8, not_3_out, or_2_out);
  and and_7 (out_6, not_4_out, or_1_out);
endmodule

module Coparator_Begin (
  input  BIT,
  input  BIT_2,
  output out_3,
  output out_4,
  output out_5
);

  wire not_1_out, not_2_out;

  not not_1 (not_1_out, BIT_2);
  not not_2 (not_2_out, BIT);
  and and_1 (out_3, BIT, not_1_out);
  xnor xnor_1 (out_4, BIT, BIT_2);
  and and_2 (out_5, not_2_out, BIT_2);
endmodule
